# Fritzing sketch lab 3 (saved by Fritzing 0.9.4)
breadboards: 1

parts:
  R1 = Resistor [tolerance=±5% resistance=220 package=THT]  # not connected
  R2 = Resistor [tolerance=±5% resistance=220 package=THT]
  R3 = Resistor [tolerance=±5% resistance=220 package=THT]  # not connected
  LED1 = RGB LED (com. cathode, rgb) [package="5 mm [THT]"]  # not connected
  Part1 = Arduino Uno (Rev3)
  R5 = Trimmer Potentiometer [maximum_resistance=10kΩ package=THT]  # not connected

nets:
  N1: R2.Pin_1, Part1.D10_PWM/SS

notes:
  *Notes*
  Rotated the potentiometer image
  220 ohms resistors
  Make sure to send power to the other side of the breadboard!
  Potentiomer from left to right: power-input-ground
